# Fritzing sketch pistol (saved by Fritzing 0.9.3b)

parts:
  S1 = Round Pushbutton
  VCC1 = Battery

nets:
  N1: S1.leg0, VCC1.+

custom parts:
  Round Pushbutton: A generic pushbutton.
  Battery: Your standard 3x 18650 battery pack (11.1 Volts)
